// Logisim project MUX.circ as structural Verilog
module MUX_1bit (
  input  S,
  input  D_0,
  input  D1,
  output out
);

  wire and_1_out, and_2_out, not_1_out;

  not not_1 (not_1_out, S);
  and and_1 (and_1_out, not_1_out, D_0);
  and and_2 (and_2_out, S, D1);
  or or_1 (out, and_1_out, and_2_out);
endmodule

module MUX_4bit (
  input  S,
  input  [3:0] A_3_0,
  input  [3:0] B_3_0,
  output [3:0] out_4
);

  MUX_1bit mux_1bit_1 (.D_0(A_3_0[3]), .D1(B_3_0[3]), .out(out_4[3]), .S(S));
  MUX_1bit mux_1bit_2 (.D_0(A_3_0[2]), .D1(B_3_0[2]), .out(out_4[2]), .S(S));
  MUX_1bit mux_1bit_3 (.D_0(A_3_0[1]), .D1(B_3_0[1]), .out(out_4[1]), .S(S));
  MUX_1bit mux_1bit_4 (.D_0(A_3_0[0]), .D1(B_3_0[0]), .out(out_4[0]), .S(S));
endmodule
