// Logisim project Counter.circ as structural Verilog: 1 circuit, main circuit main
module main (
  input  [7:0] Input,
  input  en,
  input  clk,
  input  rst,
  output [7:0] Output
);

  wire [7:0] register_1_q;

  Register register_1 (.D(Output), .en(en), .Q(register_1_q), .clk(clk), .clr(rst));
  Adder adder_1 (.a(register_1_q), .b(Input), .out(Output));  // open: cin, cout
endmodule
