// Logisim project mul.circ as structural Verilog: 1 circuit, main circuit main
module main (
  input  [3:0] in_1,
  input  [3:0] in_2,
  input  in_3,
  input  in_4,
  input  in_5,
  input  in_6,
  output out_7,
  output out_8,
  output out_9,
  output out_10,
  output out_11,
  output out_12,
  output out_13,
  output out_14
);

  wire adder_2_cout, adder_2_out, adder_3_cout, adder_3_out, adder_4_cout, adder_5_cout, adder_5_out,
       adder_6_cout, adder_7_cout, adder_7_out, adder_8_cout, adder_8_out, adder_9_cout, adder_9_out,
       adder_10_cout, adder_11_cout, adder_12_cout, and_1_out, and_2_out, and_3_out, and_4_out, and_5_out,
       and_6_out, and_7_out, and_8_out, and_9_out, and_10_out, and_11_out, and_12_out, and_13_out,
       and_14_out, and_15_out;

  and and_1 (and_1_out, in_1[3], in_2[3]);
  Adder #(.width(1)) adder_1 (.a(and_1_out), .b(adder_2_cout), .out(out_8), .cin(adder_4_cout), .cout(out_7));
  and and_2 (and_2_out, in_1[3], in_2[2]);
  Adder #(.width(1)) adder_2 (
    .a(and_2_out), .b(adder_3_cout), .out(adder_2_out), .cin(adder_5_cout), .cout(adder_2_cout));
  and and_3 (and_3_out, in_1[2], in_2[3]);
  and and_4 (and_4_out, in_1[3], in_2[1]);
  Adder #(.width(1)) adder_3 (.a(and_4_out), .b(in_4), .out(adder_3_out), .cin(adder_7_cout), .cout(adder_3_cout));
  Adder #(.width(1)) adder_4 (.a(and_3_out), .b(adder_2_out), .out(out_9), .cin(adder_6_cout), .cout(adder_4_cout));
  and and_5 (and_5_out, in_1[3], in_2[0]);
  and and_6 (and_6_out, in_1[2], in_2[2]);
  Adder #(.width(1)) adder_5 (
    .a(and_6_out), .b(adder_3_out), .out(adder_5_out), .cin(adder_8_cout), .cout(adder_5_cout));
  and and_7 (and_7_out, in_1[1], in_2[3]);
  Adder #(.width(1)) adder_6 (.a(and_7_out), .b(adder_5_out), .out(out_10), .cin(adder_10_cout), .cout(adder_6_cout));
  and and_8 (and_8_out, in_1[2], in_2[1]);
  Adder #(.width(1)) adder_7 (.a(and_8_out), .b(and_5_out), .out(adder_7_out), .cin(adder_9_cout), .cout(adder_7_cout));
  and and_9 (and_9_out, in_1[2], in_2[0]);
  and and_10 (and_10_out, in_1[1], in_2[2]);
  Adder #(.width(1)) adder_8 (
    .a(and_10_out), .b(adder_7_out), .out(adder_8_out), .cin(adder_11_cout), .cout(adder_8_cout));
  and and_11 (and_11_out, in_1[1], in_2[1]);
  Adder #(.width(1)) adder_9 (
    .a(and_11_out), .b(and_9_out), .out(adder_9_out), .cin(adder_12_cout), .cout(adder_9_cout));
  and and_12 (and_12_out, in_1[0], in_2[3]);
  Adder #(.width(1)) adder_10 (.a(and_12_out), .b(adder_8_out), .out(out_11), .cin(in_6), .cout(adder_10_cout));
  and and_13 (and_13_out, in_1[1], in_2[0]);
  and and_14 (and_14_out, in_1[0], in_2[2]);
  Adder #(.width(1)) adder_11 (.a(and_14_out), .b(adder_9_out), .out(out_12), .cin(in_5), .cout(adder_11_cout));
  and and_15 (and_15_out, in_1[0], in_2[1]);
  Adder #(.width(1)) adder_12 (.a(and_15_out), .b(and_13_out), .out(out_13), .cin(in_3), .cout(adder_12_cout));
  and and_16 (out_14, in_1[0], in_2[0]);
endmodule
